# Fritzing sketch schematics (saved by Fritzing 0.9.3b)
circuit board: 8.46667cm x 5.64444cm
breadboards: 1

parts:
  Arduino_Micro_Pro = Arduino Pro Micro (Clone)
  R1 = Trimmer Potentiometer [maximum_resistance=10kΩ package=THT]
  R2 = Trimmer Potentiometer [maximum_resistance=10kΩ package=THT]
  R4 = Trimmer Potentiometer [maximum_resistance=10kΩ package=THT]
  R3 = Trimmer Potentiometer [maximum_resistance=10kΩ package=THT]
  R7 = Trimmer Potentiometer [maximum_resistance=10kΩ package=THT]
  R8 = Trimmer Potentiometer [maximum_resistance=10kΩ package=THT]
  R5 = Trimmer Potentiometer [maximum_resistance=10kΩ package=THT]
  R6 = Trimmer Potentiometer [maximum_resistance=10kΩ package=THT]

nets:
  N1: Arduino_Micro_Pro.GND, R1.wiper, R2.wiper, R4.wiper, R3.wiper, R7.wiper, R8.wiper, R5.wiper, R6.wiper
  N2: Arduino_Micro_Pro.D4, R5.leg2
  N3: Arduino_Micro_Pro.D6, R6.leg2
  N4: Arduino_Micro_Pro.D8, R7.leg2
  N5: Arduino_Micro_Pro.D9, R8.leg2
  N6: Arduino_Micro_Pro.A0, R1.leg2
  N7: Arduino_Micro_Pro.A1, R2.leg2
  N8: Arduino_Micro_Pro.A2, R3.leg2
  N9: Arduino_Micro_Pro.A3, R4.leg2
  N10: Arduino_Micro_Pro.VCC, R1.leg1, R2.leg1, R4.leg1, R3.leg1, R7.leg1, R8.leg1, R5.leg1, R6.leg1
